# Fritzing sketch dam_remote_hydrometer (saved by Fritzing 0.9.5d)
breadboards: 1

parts:
  hc-sr1 = hc-sr04
  LED1 = LED - 5mm [color="Green (560nm)" package="5 mm [THT]"]
  Amica_NodeMCU_DevKit_1_1 = Amica NodeMCU DevKit 1.0
  R1 = Resistor [tolerance=±5% resistance=220 package="2512 [SMD]"]

nets:
  N1: hc-sr1.VCC, Amica_NodeMCU_DevKit_1_1.pin_30
  N2: hc-sr1.Trig, Amica_NodeMCU_DevKit_1_1.pin_14
  N3: hc-sr1.Echo, Amica_NodeMCU_DevKit_1_1.pin_15
  N4: hc-sr1.GND, LED1.cathode, Amica_NodeMCU_DevKit_1_1.pin2, Amica_NodeMCU_DevKit_1_1.pin_9, Amica_NodeMCU_DevKit_1_1.pin_25, Amica_NodeMCU_DevKit_1_1.pin_29
  N5: LED1.anode, R1.Pin_1
  N6: Amica_NodeMCU_DevKit_1_1.pin1, Amica_NodeMCU_DevKit_1_1.pin_10, Amica_NodeMCU_DevKit_1_1.pin_26
  N7: Amica_NodeMCU_DevKit_1_1.pin_13, R1.Pin_0

custom parts:
  Amica NodeMCU DevKit 1.0: Amica NodeMCU DEVKIT 1.0 Development Kit based on ESP8266 ESP-12E, integating GPIO, PWM, IIC, 1-Wire and ADC all in one board.
