# Fritzing sketch smart_exp_circuit (saved by Fritzing 0.9.3b)
breadboards: 2

parts:
  Componente1 = Arduino Uno (Rev3)
  R1 = Rotary Potentiometer (Small) [maximum_resistance=100kΩ package=THT]
  Led2 = LED - 5mm [color="Red (633nm)" package="5 mm [THT]"]
  Led1 = LED - 5mm [color="Green (560nm)" package="5 mm [THT]"]
  ButtonStart = Pushbutton [package="[THT]"]
  ButtonStop = Pushbutton [package="[THT]"]
  hc-sr1 = hc-sr04
  J1 = Basic Servo  # not connected
  R2 = Resistor [tolerance=±5% resistance=220 package=THT]
  R3 = Resistor [tolerance=±5% resistance=220 package=THT]
  R4 = Resistor [tolerance=±5% resistance=10k package=THT]
  R5 = Resistor [tolerance=±5% resistance=10k package=THT]

nets:
  N1: Componente1.A0, R1.wiper
  N2: Componente1.D8, hc-sr1.Trig
  N3: Componente1.D12/MISO, R2.Pin_1
  N4: Componente1.D13/SCK, R3.Pin_1
  N5: Componente1.D2, ButtonStart.Pin_3, ButtonStart.Pin_4, R5.Pin_1
  N6: Componente1.D3_PWM, ButtonStop.Pin_3, ButtonStop.Pin_4, R4.Pin_1
  N7: Componente1.D7, hc-sr1.Echo
  5V: Componente1.5V, ButtonStart.Pin_1, ButtonStart.Pin_2, ButtonStop.Pin_1, ButtonStop.Pin_2, hc-sr1.VCC
  GND: Componente1.GND, Led2.cathode, Led1.cathode, hc-sr1.GND, R4.Pin_0, R5.Pin_0
  N8: R1.leg1, R1.leg2
  N9: Led2.anode, R3.Pin_0
  N10: Led1.anode, R2.Pin_0
